# Fritzing sketch LoRa gateway RPi Zero (saved by Fritzing 0.9.3b)

parts:
  RFM95W1 = RFM95W LoRa Module
  MCU1 = Raspberry Pi Zero
  OLED1 = OLED 128x64 I2C Monochrome Display
  S1 = Pushbutton [package="[THT]"]
  S2 = Pushbutton [package="[THT]"]
  S3 = Pushbutton [package="[THT]"]

nets:
  N1: RFM95W1.2_MISO, MCU1.pin_21
  N2: RFM95W1.3_MOSI, MCU1.pin_19
  N3: RFM95W1.4_SCK, MCU1.pin_23
  N4: RFM95W1.5_NSS_(CS), MCU1.pin_26
  N5: RFM95W1.6_RESET, MCU1.pin_22
  N6: RFM95W1.10_GND, MCU1.pin_6, MCU1.pin_20, MCU1.pin_25, MCU1.pin_29, MCU1.pin_31, MCU1.pin_34, MCU1.pin_39, OLED1.GND, S1.Pin_3, S1.Pin_4, S2.Pin_3, S2.Pin_4, S3.Pin_4
  N7: RFM95W1.13_3.3V, MCU1.pin_1, MCU1.pin_17, OLED1.VDD
  N8: RFM95W1.14_DIO0, MCU1.pin_15
  N9: MCU1.pin_3, OLED1.SDA
  N10: MCU1.pin_5, OLED1.SCK
  N11: MCU1.pin_32, S3.Pin_1, S3.Pin_2

notes:
  Display OLED opcional
  Pi - RFM95
  15 - DIO0
  19 - MOSI
  21 - MISO
  22 - RST
  23 - SCK
  26 - NSS
  Botones A B C

custom parts:
  RFM95W LoRa Module: RF Transceiver by Hope RF. Well supported Arduino libraries are available. This Low Power Long Range Transceiver Module for the frequencies 868MHz and 915MHz and it is also available in other versions.
